# Fritzing sketch MyMicCircuit (saved by Fritzing 0.9.2b)
breadboards: 1

parts:
  VCC1 = Battery block 9V
  R1 = Resistor [tolerance=±5% resistance=10k package=THT]
  C1 = Ceramic Capacitor [capacitance=1µF package="0603 [SMD, multilayer]"]
  R2 = Resistor [tolerance=±5% resistance=2.6k package=THT]
  LMC6484 = IC, DIP package, 14 pins [chip_label=LMC6484]
  U2 = V_REG_LD1117VXX [package=78xxl]
  C2 = Electrolytic Capacitor [capacitance=1µF package="100 mil [THT, electrolytic]"]
  C3 = Electrolytic Capacitor [capacitance=1µF package="100 mil [THT, electrolytic]"]
  R3 = Resistor [tolerance=±5% resistance=100k package=THT]
  R4 = Resistor [tolerance=±5% resistance=22k package=THT]
  R5 = Resistor [tolerance=±5% resistance=22k package=THT]
  MSP430 = IC, DIP package, 20 pins [chip_label=MSP430]
  MIC1 = Microphone

nets:
  N1: VCC1.-, LMC6484.pin11, U2.OUT, C2.-, C3.-, R5.Pin_0, MSP430.pin20, MIC1.pin1
  N2: VCC1.+, R1.Pin_0, U2.GND, C3.+
  N3: R1.Pin_1, C1.0, MIC1.pin2
  N4: C1.1, R2.Pin_1
  N5: R2.Pin_0, LMC6484.pin13, R3.Pin_1
  N6: LMC6484.pin4, U2.IN, C2.+, R4.Pin_1, MSP430.pin1
  N7: LMC6484.pin12, R4.Pin_0, R5.Pin_1
  N8: LMC6484.pin14, R3.Pin_0, MSP430.pin15

notes:
  2.6kΩ
  10kΩ
  100kΩ
  2.2kΩ
  1µF
  3V
  P1_7
